// Logisim project HERA.circ as structural Verilog: 14 circuits, main circuit main
module main (
);

  wire clk, d_ff_1_q, LD, ST, undriven;
  wire [3:0] a, address, b, d;
  wire [4:0] F, Flags_out;
  wire [15:0] ALSU_OUT, R_1, R_2, R_3, R_a, R_b, R_d, ram_1_dout, ram_address, RAMOUT;
  wire [15:12] instruction;

  Clock u_clk (.out(clk));
  ROM #(.addrWidth(4), .dataWidth(16)) rom_1 (.addr(address), .data({instruction, d, a, b}));
  PC pc_1 (.clk(clk), .addresss(address));
  Reg_Control reg_control_1 (
    .d(d), .a(a), .b(b), .Rd(R_d), .opcode(instruction), .clk(clk), .R_1(R_1), .R_2(R_2), .R_3(R_3),
    .R_b(R_b), .R_a(R_a));
  RAM_Instructions ram_instructions_1 (
    .clk(clk), .R_b(R_b), .offset(a), .opcode(instruction), .Address(ram_address), .LD(LD), .ST(ST));
  RAM #(.addrWidth(16), .dataWidth(16), .trigger("falling")) ram_1 (
    .addr(ram_address), .we(ST), .oe(LD), .clk(clk), .din(R_b), .dout(ram_1_dout));
  DotMatrix #(.dotshape("circle"), .matrixrows(1)) dotmatrix_1 (
    .col0(F[0]), .col1(F[1]), .col2(F[2]), .col3(F[3]), .col4(F[4]));
  FlagBank flagbank_1 (.clk(clk), .flags(F), .flags_out(Flags_out));
  ALSU alsu_1 (
    .Flags(Flags_out), .R_a(R_a), .R_b(R_b), .Rd(R_d), .opcode(instruction), .d(d), .a(a), .b(b),
    .R_d(ALSU_OUT), .Flags_out(F));
  Multiplexer #(.width(16)) multiplexer_1 (.in0(ALSU_OUT), .in1(RAMOUT), .out(R_d), .sel(d_ff_1_q));
  D_Flip_Flop d_ff_1 (.D(LD), .clk(clk), .Q(d_ff_1_q), .reset(undriven));  // open: Qn, preset
  Multiplexer #(.width(16)) multiplexer_2 (.in0({16{1'b0}}), .in1(ram_1_dout), .out(RAMOUT), .sel(d_ff_1_q));
  Hex_Digit_Display hex_digit_display_1 (.value(address));  // open: dp
  Hex_Digit_Display hex_digit_display_2 ();  // open: value, dp
  Hex_Digit_Display hex_digit_display_3 (.value(instruction));  // open: dp
  Hex_Digit_Display hex_digit_display_4 (.value(d));  // open: dp
  Hex_Digit_Display hex_digit_display_5 (.value(R_1[15:12]));  // open: dp
  Hex_Digit_Display hex_digit_display_6 (.value(R_1[11:8]));  // open: dp
  Hex_Digit_Display hex_digit_display_7 (.value(R_2[15:12]));  // open: dp
  Hex_Digit_Display hex_digit_display_8 (.value(R_2[11:8]));  // open: dp
  Hex_Digit_Display hex_digit_display_9 (.value(R_3[15:12]));  // open: dp
  Hex_Digit_Display hex_digit_display_10 (.value(R_3[11:8]));  // open: dp
  Hex_Digit_Display hex_digit_display_11 (.value(ram_address[15:12]));  // open: dp
  Hex_Digit_Display hex_digit_display_12 (.value(ram_address[11:8]));  // open: dp
  Hex_Digit_Display hex_digit_display_13 (.value(RAMOUT[15:12]));  // open: dp
  Hex_Digit_Display hex_digit_display_14 (.value(RAMOUT[11:8]));  // open: dp
  Hex_Digit_Display hex_digit_display_15 ();  // open: value, dp
  Hex_Digit_Display hex_digit_display_16 (.value(a));  // open: dp
  Hex_Digit_Display hex_digit_display_17 (.value(R_1[7:4]));  // open: dp
  Hex_Digit_Display hex_digit_display_18 (.value(R_2[7:4]));  // open: dp
  Hex_Digit_Display hex_digit_display_19 (.value(R_3[7:4]));  // open: dp
  Hex_Digit_Display hex_digit_display_20 (.value(ram_address[7:4]));  // open: dp
  Hex_Digit_Display hex_digit_display_21 (.value(RAMOUT[7:4]));  // open: dp
  Hex_Digit_Display hex_digit_display_22 ();  // open: value, dp
  Hex_Digit_Display hex_digit_display_23 (.value(b));  // open: dp
  Hex_Digit_Display hex_digit_display_24 (.value(R_1[3:0]));  // open: dp
  Hex_Digit_Display hex_digit_display_25 (.value(R_2[3:0]));  // open: dp
  Hex_Digit_Display hex_digit_display_26 (.value(R_3[3:0]));  // open: dp
  Hex_Digit_Display hex_digit_display_27 (.value(ram_address[3:0]));  // open: dp
  Hex_Digit_Display hex_digit_display_28 (.value(RAMOUT[3:0]));  // open: dp

  // Other names for the same wires on the sheet: instruction[11:0] = {d, a, b}; opcode[3:0] = instruction

  // Notes on the sheet:
  //   contents of rom_1 (hex, n*v repeats v):
  //   3160 e1fe f1ff e203 a321 6112 4340 a331
  //   Register Bank
  //   Main Module for HERA Processor
  //   Flags
  //   Flag Bank
  //   Flags: Sign, Zero, Overflow, Carry, CarryBlock
  //   Address
  //   Instructions
  //   Register 1
  //   Register 2
  //   Register 3
  //   RAM Address
  //   RAM Output
endmodule

// RegBank
module RegisterBank (
  input  [15:0] R_d,
  input  [3:0] d,
  input  [3:0] a,
  input  [3:0] b,
  input  clk,
  output [15:0] R_1,
  output [15:0] R_2,
  output [15:0] R_3,
  output [15:0] R_b,
  output [15:0] R_a
);

  wire R0_in, R1_in, R2_in, R3_in, R4_in, R5_in, R6_in, R7_in, R8_in, R9_in, R10_in, R11_in, R12_in, R13_in,
       R14_in, R15_in;
  wire [15:0] R0_out, R4_out, R5_out, R6_out, R7_out, R8_out, R9_out, R10_out, R11_out, R12_out, R13_out,
       R14_out, R15_out;

  Decoder #(.select(4)) decoder_1 (
    .out0(R0_in), .out1(R1_in), .out2(R2_in), .out3(R3_in), .out4(R4_in), .out5(R5_in), .out6(R6_in),
    .out7(R7_in), .out8(R8_in), .out9(R9_in), .out10(R10_in), .out11(R11_in), .out12(R12_in), .out13(R13_in),
    .out14(R14_in), .out15(R15_in), .sel(d));  // open: en
  Register #(.width(16)) R0 (.D({16{1'b0}}), .en(R0_in), .clk(clk), .Q(R0_out));  // open: clr
  Register #(.width(16)) R4 (.D(R_d), .en(R4_in), .clk(clk), .Q(R4_out));  // open: clr
  Register #(.width(16)) R8 (.D(R_d), .en(R8_in), .clk(clk), .Q(R8_out));  // open: clr
  Register #(.width(16)) R12 (.D(R_d), .en(R12_in), .clk(clk), .Q(R12_out));  // open: clr
  Register #(.width(16)) R1 (.D(R_d), .en(R1_in), .clk(clk), .Q(R_1));  // open: clr
  Register #(.width(16)) R5 (.D(R_d), .en(R5_in), .clk(clk), .Q(R5_out));  // open: clr
  Register #(.width(16)) R9 (.D(R_d), .en(R9_in), .clk(clk), .Q(R9_out));  // open: clr
  Register #(.width(16)) R13 (.D(R_d), .en(R13_in), .clk(clk), .Q(R13_out));  // open: clr
  Register #(.width(16)) R2 (.D(R_d), .en(R2_in), .clk(clk), .Q(R_2));  // open: clr
  Register #(.width(16)) R6 (.D(R_d), .en(R6_in), .clk(clk), .Q(R6_out));  // open: clr
  Register #(.width(16)) R10 (.D(R_d), .en(R10_in), .clk(clk), .Q(R10_out));  // open: clr
  Register #(.width(16)) R14 (.D(R_d), .en(R14_in), .clk(clk), .Q(R14_out));  // open: clr
  Register #(.width(16)) R3 (.D(R_d), .en(R3_in), .clk(clk), .Q(R_3));  // open: clr
  Register #(.width(16)) R7 (.D(R_d), .en(R7_in), .clk(clk), .Q(R7_out));  // open: clr
  Register #(.width(16)) R11 (.D(R_d), .en(R11_in), .clk(clk), .Q(R11_out));  // open: clr
  Register #(.width(16)) R15 (.D(R_d), .en(R15_in), .clk(clk), .Q(R15_out));  // open: clr
  Multiplexer #(.select(4), .width(16)) multiplexer_1 (
    .in0(R0_out), .in1(R_1), .in2(R_2), .in3(R_3), .in4(R4_out), .in5(R5_out), .in6(R6_out), .in7(R7_out),
    .in8(R8_out), .in9(R9_out), .in10(R10_out), .in11(R11_out), .in12(R12_out), .in13(R13_out),
    .in14(R14_out), .in15(R15_out), .out(R_a), .sel(a));
  Multiplexer #(.select(4), .width(16)) multiplexer_2 (
    .in0(R0_out), .in1(R_1), .in2(R_2), .in3(R_3), .in4(R4_out), .in5(R5_out), .in6(R6_out), .in7(R7_out),
    .in8(R8_out), .in9(R9_out), .in10(R10_out), .in11(R11_out), .in12(R12_out), .in13(R13_out),
    .in14(R14_out), .in15(R15_out), .out(R_b), .sel(b));

  // Other names for the same wires on the sheet: R1_out[15:0] = R_1; R2_out[15:0] = R_2; R3_out[15:0] = R_3

  // Notes on the sheet:
  //   Register Bank
  //   Register bank containing 16 16-bit registers
  //   We can read two registers R_a and R_b and write to R_d
endmodule

// Reg_Bank
module Reg_Control (
  input  [3:0] d,
  input  [3:0] a,
  input  [3:0] b,
  input  [15:0] Rd,
  input  [3:0] opcode,
  input  clk,
  output [15:0] R_1,
  output [15:0] R_2,
  output [15:0] R_3,
  output [15:0] R_b,
  output [15:0] R_a
);

  wire and_1_out, comparator_1_eq;
  wire [3:0] multiplexer_1_out, multiplexer_2_out, multiplexer_3_out, register_1_q, undriven;

  Multiplexer #(.select(4), .width(4)) multiplexer_1 (
    .in0(undriven), .in1(undriven), .in2(undriven), .in3(undriven), .in4(undriven), .in5(undriven),
    .in6(undriven), .in7(d), .in8(d), .in9(d), .in10(d), .in11(d), .in12(d), .in13(d), .in14(d), .in15(d),
    .out(multiplexer_1_out), .sel(a));
  Multiplexer #(.select(4), .width(4)) multiplexer_2 (
    .in0(a), .in1(a), .in2(a), .in3(multiplexer_1_out), .in4(a), .in5(a), .in6(a), .in7(a), .in8(a), .in9(a),
    .in10(a), .in11(a), .in12(a), .in13(a), .in14(a), .in15(a), .out(multiplexer_2_out), .sel(opcode));
  Register #(.width(4)) register_1 (.D(d), .clk(clk), .Q(register_1_q), .clr(and_1_out));  // open: en
  Comparator #(.width(4)) comparator_1 (.a(opcode), .b(4'b0100), .eq(comparator_1_eq));  // open: gt, lt
  RegisterBank registerbank_1 (
    .R_d(Rd), .d(multiplexer_3_out), .a(multiplexer_2_out), .b(b), .clk(clk), .R_1(R_1), .R_2(R_2),
    .R_3(R_3), .R_b(R_b), .R_a(R_a));
  and and_1 (and_1_out, comparator_1_eq, ~clk);  // AND_Gate
  Multiplexer #(.select(3), .width(4)) multiplexer_3 (
    .in0(d), .in1(d), .in2(register_1_q), .in3(4'b0000), .in4(d), .in5(d), .in6(d), .in7(d),
    .out(multiplexer_3_out), .sel(opcode[3:1]));

  // Other names for the same wires on the sheet: R_d[15:0] = Rd

  // Notes on the sheet:
  //   Saving and Restoring flags
endmodule

module ALSU (
  input  [4:0] Flags,
  input  [15:0] R_a,
  input  [15:0] R_b,
  input  [15:0] Rd,
  input  [3:0] opcode,
  input  [3:0] d,
  input  [3:0] a,
  input  [3:0] b,
  output [15:0] R_d,
  output [4:0] Flags_out
);

  wire [4:0] F_arith, F_bitwise, F_inc_dec, F_set, F_Shift, multiplexer_4_out, multiplexer_5_out;
  wire [15:0] arith, bit_extender_2_out, bw, I_D, multiplexer_1_out, multiplexer_2_out, setlo, Shift;

  assign setlo = {{8{a[3]}}, {a, b}};  // Bit_Extender bit_extender_1
  Bitwise bitwise_1 (.R_a(R_a), .R_b(R_b), .op(opcode[2:0]), .Flags_in(Flags), .R_d(bw), .Flags_out(F_bitwise));
  Arithmetic arithmetic_1 (.R_a(R_a), .R_b(R_b), .op(opcode[2:0]), .Flags_in(Flags), .R_d(arith), .Flags_out(F_arith));
  assign bit_extender_2_out = {{11{1'b0}}, Flags};  // Bit_Extender bit_extender_2
  Multiplexer #(.width(16)) multiplexer_1 (.in0(bit_extender_2_out), .in1(R_a), .out(multiplexer_1_out), .sel(b[3]));
  Multiplexer #(.select(4), .width(16)) multiplexer_2 (
    .in0(Shift), .in1(Shift), .in2(Shift), .in3(Shift), .in4(Shift), .in5(Shift), .in6({16{1'b0}}),
    .in7(multiplexer_1_out), .in8(I_D), .in9(I_D), .in10(I_D), .in11(I_D), .in12(I_D), .in13(I_D),
    .in14(I_D), .in15(I_D), .out(multiplexer_2_out), .sel(a));
  LS ls_1 (.R_b_in(R_b), .op(a[2:0]), .Flags_in(Flags), .R_b_out(Shift), .Flags_out(F_Shift));
  INC_DEC inc_dec_1 (.R_d(R_a), .epsilon({a[1:0], b}), .op(a[2]), .Flags_in(Flags), .res(I_D), .Flags_out(F_inc_dec));
  Flag_Set flag_set_1 (
    .opcode(d[3:1]), .Fin_instruction({d[0], b}), .Flags_in(Flags), .Flags_out(F_set));  // open: out_5
  Multiplexer #(.select(4), .width(16)) multiplexer_3 (
    .in0({16{1'b0}}), .in1({16{1'b0}}), .in2({16{1'b0}}), .in3(multiplexer_2_out), .in4({16{1'b0}}),
    .in5({16{1'b0}}), .in6({16{1'b0}}), .in7({16{1'b0}}), .in8(bw), .in9(bw), .in10(arith), .in11(arith),
    .in12(arith), .in13(bw), .in14(setlo), .in15({a, b, Rd[7:0]}), .out(R_d), .sel(opcode));
  Multiplexer #(.width(5)) multiplexer_4 (.in0(Flags), .in1(R_a[4:0]), .out(multiplexer_4_out), .sel(b[3]));
  Multiplexer #(.select(4), .width(5)) multiplexer_5 (
    .in0(F_Shift), .in1(F_Shift), .in2(F_Shift), .in3(F_Shift), .in4(F_Shift), .in5(F_Shift), .in6(F_set),
    .in7(multiplexer_4_out), .in8(F_inc_dec), .in9(F_inc_dec), .in10(F_inc_dec), .in11(F_inc_dec),
    .in12(F_inc_dec), .in13(F_inc_dec), .in14(F_inc_dec), .in15(F_inc_dec), .out(multiplexer_5_out), .sel(a));
  Multiplexer #(.select(4), .width(5)) multiplexer_6 (
    .in0(Flags), .in1(Flags), .in2(Flags), .in3(multiplexer_5_out), .in4(Flags), .in5(Flags), .in6(Flags),
    .in7(Flags), .in8(F_bitwise), .in9(F_bitwise), .in10(F_arith), .in11(F_arith), .in12(F_arith),
    .in13(F_bitwise), .in14(Flags), .in15(Flags), .out(Flags_out), .sel(opcode));

  // Other names for the same wires on the sheet: sethi[15:0] = {a, b, Rd[7:0]}; F[4:0] = Flags

  // Notes on the sheet:
  //   ALSU
  //   SETLO logic
  //   Bitwise instructions (AND, OR, XOR)
  //   Arithmetic instructions (ADD, SUB, MUL)
  //   11:8
  //   7:4
  //   3:0
  //   SAVEF
  //   15:12
  //   Module that handles arithmetic and other operations done on values stored in register bank
  //   Flag Instructions
  //   Flag opcode
  //   Input Flags
  //   Increment and Decrement (INC, DEC)
  //   Manually setting flags (FON, FOFF, FSET4, FSET5)
  //   Shift Instructions (LSL, LSR, LSL8, LSR8, ASL, ASR)
endmodule

module PC (
  input  clk,
  output [3:0] addresss
);

  Counter #(.max('hf), .width(4)) counter_1 (.clk(clk), .Q(addresss));  // open: clr, load, up, count, D, carry

  // Notes on the sheet:
  //   Program counter:  
  //   We read through four bit addresses that are fed into our ROM to retrieve instructions for the CPU. 
endmodule

// Flags
module FlagBank (
  input  clk,
  input  [4:0] flags,
  output [4:0] flags_out
);

  wire reset;

  D_Flip_Flop Sign (.D(flags[0]), .clk(clk), .Q(flags_out[0]), .reset(reset));  // open: Qn, preset
  D_Flip_Flop Carry (.D(flags[3]), .clk(clk), .Q(flags_out[3]), .reset(reset));  // open: Qn, preset
  D_Flip_Flop Zero (.D(flags[1]), .clk(clk), .Q(flags_out[1]), .reset(reset));  // open: Qn, preset
  D_Flip_Flop Carryblock (.D(flags[4]), .clk(clk), .Q(flags_out[4]), .reset(reset));  // open: Qn, preset
  D_Flip_Flop Overflow (.D(flags[2]), .clk(clk), .Q(flags_out[2]), .reset(reset));  // open: Qn, preset

  // Other names for the same wires on the sheet: F0 = flags[0]; F1 = flags[1]; F2 = flags[2]; F3 = flags[3];
  //   F4 = flags[4]; F0_out = flags_out[0]; F1_out = flags_out[1]; F2_out = flags_out[2]; F3_out = flags_out[3];
  //   F4_out = flags_out[4]

  // Notes on the sheet:
  //   Flag bank: consists of five D-flip flops to store the current state of each flag
endmodule

// F_Set
module Flag_Set (
  input  [2:0] opcode,
  input  [4:0] Fin_instruction,
  input  [4:0] Flags_in,
  output [4:0] Flags_out,
  output [4:0] out_5
);

  wire [4:0] FON, undriven;

  assign FON = Fin_instruction | Flags_in;  // OR_Gate or_1, 5 bits wide
  assign out_5 = Flags_in & ~Fin_instruction;  // AND_Gate and_1, 5 bits wide
  Multiplexer #(.select(3), .width(5)) multiplexer_1 (
    .in0(FON), .in1(Flags_in), .in2(Fin_instruction), .in3(Flags_in), .in4(out_5), .in5(Flags_in),
    .in6({Flags_in[4], Fin_instruction[3:0]}), .in7(undriven), .out(Flags_out), .sel(opcode));

  // Other names for the same wires on the sheet: FOFF[4:0] = out_5; FSET4[4:0] = {Flags_in[4], Fin_instruction[3:0]};
  //   FSET5[4:0] = Fin_instruction; cb_flag = Flags_in[4]

  // Notes on the sheet:
  //   Manually Setting Flags
  //   Given the instructions, we can manually turn on and off flags.
  //   FSET4 leaves carry block flag unchanged 
endmodule

module LS (
  input  [15:0] R_b_in,
  input  [2:0] op,
  input  [4:0] Flags_in,
  output [15:0] R_b_out,
  output [4:0] Flags_out
);

  wire and_1_out, and_2_out, comparator_2_eq, decoder_1_out0, decoder_1_out1, decoder_1_out4, decoder_1_out5,
       h, high_res, or_1_out, or_2_out;
  wire [14:0] multiplexer_1_out, shifter_1_out, shifter_2_out_2;
  wire [14:14] multiplexer_1_out_2;
  wire [15:0] LSL8, LSR8;
  wire [15:15] shifter_2_out;

  Decoder #(.select(3)) decoder_1 (
    .out0(decoder_1_out0), .out1(decoder_1_out1), .out4(decoder_1_out4), .out5(decoder_1_out5), .sel(op));  // open: out2, out3, out6, out7, en
  Comparator #(.width(16)) comparator_1 (
    .a(R_b_out), .b({16{1'b0}}), .eq(Flags_out[1]), .lt(Flags_out[0]));  // open: gt
  xor xor_1 (Flags_out[2], R_b_in[15], high_res);
  or or_1 (or_1_out, decoder_1_out0, decoder_1_out4);
  or or_2 (or_2_out, decoder_1_out1, decoder_1_out5);
  Shifter #(.width(16)) shifter_1 (.in(R_b_in), .\dist (4'b0001), .out({h, shifter_1_out}));
  Shifter #(.shift("lr"), .width(16)) shifter_2 (
    .in(R_b_in), .\dist (4'b0001), .out({shifter_2_out[15], shifter_2_out_2}));
  Shifter #(.width(16)) shifter_3 (.in(R_b_in), .\dist (4'b1000), .out(LSL8));
  Shifter #(.shift("lr"), .width(16)) shifter_4 (.in(R_b_in), .\dist (4'b1000), .out(LSR8));
  and and_1 (and_1_out, R_b_in[15], or_1_out);
  and and_2 (and_2_out, R_b_in[0], or_2_out);
  or or_3 (Flags_out[3], and_1_out, and_2_out);
  Multiplexer #(.select(3), .width(16)) multiplexer_1 (
    .in0({h, shifter_1_out}), .in1({shifter_2_out[15], shifter_2_out_2}), .in4({h, shifter_1_out}),
    .in5({R_b_in[15], shifter_2_out_2}), .in6({16{1'b0}}), .in7({16{1'b0}}),
    .out({multiplexer_1_out_2[14], multiplexer_1_out}), .sel(op));  // open: in2, in3
  Comparator #(.width(3)) comparator_2 (.a(op), .b(3'b100), .eq(comparator_2_eq));  // open: gt, lt
  Multiplexer multiplexer_2 (.in0(1'b0), .in1(h), .out(high_res), .sel(comparator_2_eq));
  Multiplexer #(.select(3), .width(16)) multiplexer_3 (
    .in0({multiplexer_1_out_2[14], multiplexer_1_out[14:1], Flags_out[3]}),
    .in1({Flags_out[3], multiplexer_1_out}), .in2({multiplexer_1_out_2[14], multiplexer_1_out}),
    .in3({multiplexer_1_out_2[14], multiplexer_1_out}),
    .in4({multiplexer_1_out_2[14], multiplexer_1_out[14:1], Flags_out[3]}),
    .in5({Flags_out[3], multiplexer_1_out}), .in6({16{1'b0}}), .in7({16{1'b0}}), .out(R_b_out), .sel(op));

  assign Flags_out[4] = Flags_in[4];

  // Other names for the same wires on the sheet: high = R_b_in[15]; c_out = Flags_out[3]; R_b[15:0] = R_b_out;
  //   low = R_b_in[0]

  // Notes on the sheet:
  //   Logical Shift Operations
  //   Module for performing various logical shift operations on the value stored in a given register 
  //   Logical Shift Left
  //   Logical Shift Right
  //   Logical Shift Left 8-bits
  //   Logical Shift Right 8-bits
  //   check if bit is 1 on far left or right: if yes then depending on whether its a logical shift right or left then turn on carry flag 
  //   shift in carry bit for LSL, LSR, and ASL
  //   overflow flag set
endmodule

// INC/DEC
module INC_DEC (
  input  [15:0] R_d,
  input  [5:0] epsilon,
  input  op,
  input  [4:0] Flags_in,
  output [15:0] res,
  output [4:0] Flags_out
);

  wire c14;
  wire [1:0] c_add, c_sub;
  wire [5:0] adder_1_out, adder_2_out;
  wire [15:0] bit_extender_1_out, bit_extender_2_out, dec, inc, not_1_out;

  Adder #(.width(6)) adder_1 (.a(epsilon), .b(6'b000001), .out(adder_1_out));  // open: cin, cout
  Adder #(.width(6)) adder_2 (.a(epsilon), .b(6'b000001), .out(adder_2_out));  // open: cin, cout
  assign bit_extender_1_out = {{10{adder_1_out[5]}}, adder_1_out};  // Bit_Extender bit_extender_1
  assign bit_extender_2_out = {{10{adder_2_out[5]}}, adder_2_out};  // Bit_Extender bit_extender_2
  assign not_1_out = ~bit_extender_1_out;  // NOT_Gate not_1, 16 bits wide
  xor xor_1 (Flags_out[2], Flags_out[3], c14);
  ADD add_1 (.c_in(1'b0), .R_a(R_d), .R_b(bit_extender_2_out), .sum(inc), .c_out(c_add));
  ADD add_2 (.c_in(1'b1), .R_a(R_d), .R_b(not_1_out), .sum(dec), .c_out(c_sub));
  Multiplexer #(.width(16)) multiplexer_1 (.in0(inc), .in1(dec), .out({Flags_out[0], res[14:0]}), .sel(op));
  Multiplexer #(.width(2)) multiplexer_2 (.in0(c_add), .in1(c_sub), .out({Flags_out[3], c14}), .sel(op));
  Comparator #(.width(16)) comparator_1 (
    .a({Flags_out[0], res[14:0]}), .b({16{1'b0}}), .eq(Flags_out[1]));  // open: gt, lt

  assign Flags_out[4] = Flags_in[4];
  assign res[15] = Flags_out[0];

  // Other names for the same wires on the sheet: c15 = Flags_out[3]; F_in[4:0] = Flags_in; z = Flags_out[1];
  //   s = Flags_out[0]

  // Notes on the sheet:
  //   Increment/Decrement
endmodule

module Bitwise (
  input  [15:0] R_a,
  input  [15:0] R_b,
  input  [2:0] op,
  input  [4:0] Flags_in,
  output [15:0] R_d,
  output [4:0] Flags_out
);

  wire [15:0] AND, OR, XOR;

  assign AND = R_a & R_b;  // AND_Gate AND, 16 bits wide
  assign OR = R_a | R_b;  // OR_Gate OR, 16 bits wide
  assign XOR = R_a ^ R_b;  // XOR_Gate XOR, 16 bits wide
  Multiplexer #(.select(3), .width(16)) multiplexer_1 (
    .in0(AND), .in1(OR), .in5(XOR), .out({Flags_out[0], R_d[14:0]}), .sel(op));  // open: in2, in3, in4, in6, in7
  Comparator #(.width(16)) comparator_1 (
    .a({Flags_out[0], R_d[14:0]}), .b({16{1'b0}}), .eq(Flags_out[1]));  // open: gt, lt

  assign Flags_out[4:2] = Flags_in[4:2];
  assign R_d[15] = Flags_out[0];

  // Other names for the same wires on the sheet: z = Flags_out[1]; s = Flags_out[0]

  // Notes on the sheet:
  //   Bitwise instructions 
  //   AND logic
  //   OR logic
  //   XOR logic
  //   set s to B_15 of the result
endmodule

module Arithmetic (
  input  [15:0] R_a,
  input  [15:0] R_b,
  input  [2:0] op,
  input  [4:0] Flags_in,
  output [15:0] R_d,
  output [4:0] Flags_out
);

  wire c14, comparator_1_eq, not_2_out, xor_1_out;
  wire [1:0] c_add, c_sub;
  wire [15:0] A, L_MUL, not_1_out, SUB, U_MUL;
  wire [31:0] bit_extender_1_out;

  Multiplier #(.width(16)) multiplier_1 (.a(R_a), .b(R_b), .out(L_MUL), .cout(U_MUL));  // open: cin
  assign bit_extender_1_out = {{15{1'b0}}, {Flags_out[0], L_MUL}};  // Bit_Extender bit_extender_1
  xor xor_1 (xor_1_out, Flags_out[3], c14);
  assign not_1_out = ~R_b;  // NOT_Gate not_1, 16 bits wide
  Comparator #(.width(32)) comparator_1 (
    .a({U_MUL, L_MUL}), .b(bit_extender_1_out), .eq(comparator_1_eq));  // open: gt, lt
  ADD add_1 (.c_in(1'b0), .R_a(R_a), .R_b(R_b), .sum(A), .c_out(c_add));
  ADD add_2 (.c_in(1'b1), .R_a(R_a), .R_b(not_1_out), .sum(SUB), .c_out(c_sub));
  Multiplexer #(.select(3)) multiplexer_1 (
    .in0(1'b0), .in1(1'b0), .in2(xor_1_out), .in3(xor_1_out), .in4(not_2_out), .in5(1'b0), .in6(1'b0),
    .in7(1'b0), .out(Flags_out[2]), .sel(op));
  not not_2 (not_2_out, comparator_1_eq);
  Comparator #(.width(5)) comparator_2 (.a(Flags_in), .b({5{1'b0}}));  // open: gt, eq, lt
  Multiplexer #(.select(3), .width(16)) multiplexer_2 (
    .in0({16{1'b0}}), .in1({16{1'b0}}), .in2(A), .in3(SUB), .in4(U_MUL), .in5({16{1'b0}}), .in6({16{1'b0}}),
    .in7({16{1'b0}}), .out({Flags_out[0], R_d[14:0]}), .sel(op));
  Multiplexer #(.select(3), .width(2)) multiplexer_3 (
    .in0(2'b00), .in1(2'b00), .in2(c_add), .in3(c_sub), .in4(2'b00), .in5(2'b00), .in6(2'b00), .in7(2'b00),
    .out({Flags_out[3], c14}), .sel(op));
  Comparator #(.width(16)) comparator_3 (
    .a({Flags_out[0], R_d[14:0]}), .b({16{1'b0}}), .eq(Flags_out[1]));  // open: gt, lt

  assign Flags_out[4] = Flags_in[4];
  assign R_d[15] = Flags_out[0];

  // Other names for the same wires on the sheet: c15 = Flags_out[3]; F_in[4:0] = Flags_in; z = Flags_out[1];
  //   s = Flags_out[0]; SUB_013[13:0] = SUB[13:0]; SUB_14 = SUB[14]; SUB_15 = SUB[15]

  // Notes on the sheet:
  //   SUB logic
  //   Arithmetic Instructions (ADD, SUB, MUL)
  //   ADD logic
  //   MUL logic
endmodule

module ADD (
  input  c_in,
  input  [15:0] R_a,
  input  [15:0] R_b,
  output [15:0] sum,
  output [1:0] c_out
);

  wire adder_1_cout;

  Adder #(.width(14)) adder_1 (.a(R_a[13:0]), .b(R_b[13:0]), .out(sum[13:0]), .cin(c_in), .cout(adder_1_cout));
  Adder #(.width(1)) adder_2 (.a(R_a[14]), .b(R_b[14]), .out(sum[14]), .cin(adder_1_cout), .cout(c_out[0]));
  Adder #(.width(1)) adder_3 (.a(R_a[15]), .b(R_b[15]), .out(sum[15]), .cin(c_out[0]), .cout(c_out[1]));

  // Other names for the same wires on the sheet: ADD_13[13:0] = sum[13:0]; ADD_14 = sum[14]; ADD_15 = sum[15]

  // Notes on the sheet:
  //   Carry In
  //   Add Module: Peforms addition and subtraction on R_a and R_b
  //   Carry Out
endmodule

module CarryBlock (
);


  // Notes on the sheet:
  //   Carry Block Arithmetic
endmodule

// RAM Instructions
module RAM_Instructions (
  input  clk,
  input  [15:0] R_b,
  input  [3:0] offset,
  input  [3:0] opcode,
  output [15:0] Address,
  output LD,
  output ST
);

  wire LD_t;
  wire [15:0] bit_extender_1_out;

  assign bit_extender_1_out = {{11{opcode[0]}}, {opcode[0], offset}};  // Bit_Extender bit_extender_1
  and and_1 (LD, ~opcode[1], opcode[2], ~opcode[3]);  // AND_Gate
  and and_2 (ST, opcode[1], opcode[2], ~opcode[3]);  // AND_Gate
  Adder #(.width(16)) adder_1 (.a(R_b), .b(bit_extender_1_out), .out(Address));  // open: cin, cout
  Register #(.width(16)) register_1 (.en(ST), .clk(clk));  // open: D, Q, clr
  D_Flip_Flop #(.trigger("falling")) d_ff_1 (.D(LD_t), .clk(clk));  // open: Q, Qn, preset, reset

  // Notes on the sheet:
  //   RAM Instructions
endmodule
